// Logisim project ckg-lab5.circ as structural Verilog: 1 circuit, main circuit main
module main (
  input  S,
  input  H,
  input  A,
  input  B,
  output E
);

  wire and_1_out, and_2_out, not_1_out;

  not not_1 (not_1_out, A);
  and and_1 (and_1_out, A, B);
  and and_2 (and_2_out, S, not_1_out);
  or or_1 (E, and_2_out, H, and_1_out);

  // Notes on the sheet:
  //   Didgey Talgoic
endmodule
