// Logisim project S-R Flip-Flop.circ as structural Verilog: 1 circuit, main circuit main
module main (
  input  S,
  input  R,
  output QBar,
  output Q
);

  nor nor_1 (QBar, S, Q);
  nor nor_2 (Q, R, QBar);
endmodule
