// Logisim project CKG_1.circ as structural Verilog: 1 circuit, main circuit main
module main (
  input  A,
  input  C,
  input  A_2,
  input  A_3,
  input  C_2,
  input  B,
  input  D,
  input  C_3,
  input  B_2,
  input  A_4,
  input  D_2,
  input  A_5,
  input  B_3,
  input  B_4,
  input  A_6,
  input  C_4,
  input  C_5,
  input  D_3,
  input  B_5,
  input  D_4,
  output out_21,
  output out_22,
  output out_23
);

  wire and_1_out, and_2_out, and_3_out, and_4_out, and_5_out, and_6_out, and_7_out, and_8_out, and_9_out,
       not_1_out, not_2_out, not_3_out, not_4_out, not_5_out, not_6_out, not_7_out, not_8_out, not_9_out,
       not_10_out, not_11_out;

  not not_1 (not_1_out, A);
  not not_2 (not_2_out, C_2);
  not not_3 (not_3_out, B_3);
  not not_4 (not_4_out, C_5);
  not not_5 (not_5_out, D_4);
  and and_1 (and_1_out, not_1_out, C);
  and and_2 (and_2_out, A_2, not_2_out);
  and and_3 (and_3_out, A_4, not_3_out);
  and and_4 (and_4_out, A_6, not_4_out);
  and and_5 (and_5_out, B_5, not_5_out);
  or or_1 (out_21, and_1_out, and_2_out);
  or or_2 (out_23, and_3_out, and_4_out, and_5_out);
  not not_6 (not_6_out, D);
  not not_7 (not_7_out, B_2);
  not not_8 (not_8_out, A_5);
  not not_9 (not_9_out, B_4);
  not not_10 (not_10_out, C_4);
  not not_11 (not_11_out, D_3);
  and and_6 (and_6_out, A_3, B, not_6_out);
  and and_7 (and_7_out, C_3, not_7_out, D_2);
  and and_8 (and_8_out, not_8_out, not_9_out);
  and and_9 (and_9_out, not_10_out, not_11_out);
  or or_3 (out_22, and_6_out, and_7_out, and_8_out, and_9_out);

  // Notes on the sheet:
  //   F0
  //   S
  //   F1
endmodule
