// Logisim project Adders and Subtractors.circ as structural Verilog: 1 circuit, main circuit main
module main (
  input  Q2,
  input  Q1,
  input  A,
  input  B,
  input  B_2,
  input  C,
  input  D,
  input  C_2,
  input  in_9,
  input  Q1_2,
  input  A_2,
  input  B_3,
  output out_13,
  output out_14,
  output out_15
);

  wire and_1_out, and_2_out, and_4_out, and_5_out, and_6_out, and_7_out, and_8_out, and_9_out, not_1_out,
       not_2_out, not_3_out, not_4_out, not_5_out, or_1_out, or_2_out, or_4_out, xor_1_out, xor_2_out,
       xor_3_out, xor_4_out, xor_5_out, xor_6_out, xor_8_out;

  not not_1 (not_1_out, A);
  not not_2 (not_2_out, C);
  xor xor_1 (xor_1_out, A, B);
  and and_1 (and_1_out, B, not_1_out);
  xor xor_2 (xor_2_out, A_2, B_3);
  and and_2 (and_2_out, B_3, A_2);
  not not_3 (not_3_out, Q1);
  and and_3 (out_15, B_2, not_2_out);
  xor xor_3 (xor_3_out, Q1, xor_1_out);
  and and_4 (and_4_out, xor_1_out, not_3_out);
  xor xor_4 (xor_4_out, Q1_2, xor_2_out);
  and and_5 (and_5_out, xor_2_out, Q1_2);
  or or_1 (or_1_out, and_4_out, and_1_out);
  or or_2 (or_2_out, and_5_out, and_2_out);
  not not_4 (not_4_out, xor_3_out);
  xor xor_5 (xor_5_out, xor_3_out, or_1_out);
  and and_6 (and_6_out, or_1_out, not_4_out);
  xor xor_6 (xor_6_out, xor_4_out, or_2_out);
  and and_7 (and_7_out, or_2_out, xor_4_out);
  not not_5 (not_5_out, Q2);
  xor xor_7 (out_13, Q2, xor_5_out);
  and and_8 (and_8_out, xor_5_out, not_5_out);
  xor xor_8 (xor_8_out, in_9, xor_6_out);
  and and_9 (and_9_out, xor_6_out, in_9);
  or or_3 (out_14, and_8_out, and_6_out);
  or or_4 (or_4_out, and_9_out, and_7_out);
  // NOT_Gate not_6 is placed but not wired

  // Notes on the sheet:
  //   Full Subtractor
  //   Full Adder
endmodule
