// Logisim project CKG_001.circ as structural Verilog: 1 circuit, main circuit main
module main (
  input  D,
  input  C,
  input  B,
  input  A,
  output S,
  output F1,
  output F0
);

  wire and_1_out, and_2_out, and_3_out, and_4_out, and_5_out, and_6_out, and_7_out, and_8_out, and_9_out,
       not_1_out, not_2_out, not_3_out, not_4_out;

  not not_1 (not_1_out, D);
  not not_2 (not_2_out, C);
  not not_3 (not_3_out, B);
  not not_4 (not_4_out, A);
  and and_1 (and_1_out, not_1_out, not_2_out, A);
  and and_2 (and_2_out, not_2_out, B, A);
  and and_3 (and_3_out, not_1_out, B);
  and and_4 (and_4_out, not_1_out, not_2_out, B);
  and and_5 (and_5_out, not_1_out, B, A);
  and and_6 (and_6_out, D, not_3_out, not_4_out);
  and and_7 (and_7_out, D, C, not_3_out);
  buf and_8 (and_8_out, A);  // AND_Gate
  buf and_9 (and_9_out, C);  // AND_Gate
  or or_1 (F0, and_8_out, and_9_out);
  or or_2 (S, and_1_out, and_2_out, and_3_out);
  or or_3 (F1, and_4_out, and_5_out, and_6_out, and_7_out);
endmodule
