// Logisim project CKG_01.circ as structural Verilog: 1 circuit, main circuit main
module main (
  input  A,
  input  A_2,
  input  C,
  input  B,
  input  C_2,
  input  D,
  input  A_3,
  input  B_2,
  input  C_3,
  input  D_2,
  output out_11,
  output out_12,
  output out_13
);

  wire and_1_out, and_2_out, and_3_out, and_4_out, and_5_out, and_6_out, and_7_out, and_8_out, and_9_out,
       not_1_out, not_2_out, not_3_out, not_4_out, not_5_out, not_6_out, not_7_out, not_8_out, not_9_out,
       not_10_out, not_11_out;

  not not_1 (not_1_out, A);
  not not_2 (not_2_out, C);
  not not_3 (not_3_out, B_2);
  not not_4 (not_4_out, C_3);
  not not_5 (not_5_out, D_2);
  and and_1 (and_1_out, not_1_out, C);
  and and_2 (and_2_out, A, not_2_out);
  and and_3 (and_3_out, A_3, not_3_out);
  and and_4 (and_4_out, A_3, not_4_out);
  and and_5 (and_5_out, B_2, not_5_out);
  or or_1 (out_11, and_1_out, and_2_out);
  or or_2 (out_13, and_3_out, and_4_out, and_5_out);
  not not_6 (not_6_out, D);
  not not_7 (not_7_out, B);
  not not_8 (not_8_out, A_2);
  not not_9 (not_9_out, B);
  not not_10 (not_10_out, C_2);
  not not_11 (not_11_out, D);
  and and_6 (and_6_out, A_2, B, not_6_out);
  and and_7 (and_7_out, C_2, not_7_out, D);
  and and_8 (and_8_out, not_8_out, not_9_out);
  and and_9 (and_9_out, not_10_out, not_11_out);
  or or_3 (out_12, and_6_out, and_7_out, and_8_out, and_9_out);

  // Notes on the sheet:
  //   F0
  //   S
  //   F1
endmodule
