// Logisim project Logism_2.circ as structural Verilog: 1 circuit, main circuit main
module main (
  input  [3:0] P,
  input  [3:0] Q,
  input  [2:0] F2F1F0,
  output [3:0] F
);

  wire comparator_1_eq, comparator_2_eq, comparator_3_eq, comparator_4_eq, comparator_5_eq, comparator_6_eq,
       comparator_7_eq, comparator_8_eq;
  wire [3:0] adder_1_out, adder_2_out, adder_3_out, subtractor_1_out, subtractor_2_out, subtractor_3_out;

  Adder #(.width(4)) adder_1 (.a(P), .b(4'b0001), .out(adder_1_out));  // open: cin, cout
  Adder #(.width(4)) adder_2 (.a(P), .b(4'b0001), .out(adder_2_out));  // open: cin, cout
  Subtractor #(.width(4)) subtractor_1 (.a(P), .b(4'b0001), .out(subtractor_1_out));  // open: bin, bout
  Subtractor #(.width(4)) subtractor_2 (.a(Q), .b(4'b0001), .out(subtractor_2_out));  // open: bin, bout
  Adder #(.width(4)) adder_3 (.a(P), .b(Q), .out(adder_3_out));  // open: cin, cout
  Subtractor #(.width(4)) subtractor_3 (.a(Q), .b(P), .out(subtractor_3_out));  // open: bin, bout
  Comparator #(.width(3)) comparator_1 (.a(F2F1F0), .b(3'b000), .eq(comparator_1_eq));  // open: gt, lt
  Comparator #(.width(3)) comparator_2 (.a(F2F1F0), .b(3'b001), .eq(comparator_2_eq));  // open: gt, lt
  Comparator #(.width(3)) comparator_3 (.a(F2F1F0), .b(3'b010), .eq(comparator_3_eq));  // open: gt, lt
  Comparator #(.width(3)) comparator_4 (.a(F2F1F0), .b(3'b011), .eq(comparator_4_eq));  // open: gt, lt
  Comparator #(.width(3)) comparator_5 (.a(F2F1F0), .b(3'b100), .eq(comparator_5_eq));  // open: gt, lt
  Comparator #(.width(3)) comparator_6 (.a(F2F1F0), .b(3'b101), .eq(comparator_6_eq));  // open: gt, lt
  Comparator #(.width(3)) comparator_7 (.a(F2F1F0), .b(3'b110), .eq(comparator_7_eq));  // open: gt, lt
  Comparator #(.width(3)) comparator_8 (.a(F2F1F0), .b(3'b111), .eq(comparator_8_eq));  // open: gt, lt
  assign F = comparator_1_eq ? P : 4'bz;  // Controlled_Buffer controlled_buffer_1
  assign F = comparator_2_eq ? Q : 4'bz;  // Controlled_Buffer controlled_buffer_2
  assign F = comparator_3_eq ? adder_1_out : 4'bz;  // Controlled_Buffer controlled_buffer_3
  assign F = comparator_4_eq ? adder_2_out : 4'bz;  // Controlled_Buffer controlled_buffer_4
  assign F = comparator_5_eq ? subtractor_1_out : 4'bz;  // Controlled_Buffer controlled_buffer_5
  assign F = comparator_6_eq ? subtractor_2_out : 4'bz;  // Controlled_Buffer controlled_buffer_6
  assign F = comparator_7_eq ? adder_3_out : 4'bz;  // Controlled_Buffer controlled_buffer_7
  assign F = comparator_8_eq ? subtractor_3_out : 4'bz;  // Controlled_Buffer controlled_buffer_8
endmodule
